# Fritzing sketch MICRO_Adafruit_GPS_OLED (saved by Fritzing 0.8.7b)
breadboards: 1

parts:
  ARDUINO1 = Arduino Micro
  GPS1 = Adafruit Ultimate GPS Breakout
  OLED1 = 128x64 Monochrom OLED Display with SPI Control

nets:
  N1: ARDUINO1.TX, GPS1.RX
  N2: ARDUINO1.RX, GPS1.TX
  GND: ARDUINO1.GND#6, GPS1.GND, OLED1.GND
  N3: ARDUINO1.D9, OLED1.Data
  N4: ARDUINO1.D10, OLED1.Clock
  N5: ARDUINO1.D11, OLED1.SA0/DC
  N6: ARDUINO1.D12, OLED1.CS
  N7: ARDUINO1.D13, OLED1.Reset
  VIN: ARDUINO1.5V, GPS1.VIN, OLED1.Vin

notes:
  Arduino MICRO and Adafruit's Ultimate GPS chipset. OLED uses SPI interface and GPS uses softwre serial. brycej 02/24/2014

custom parts:
  Arduino Micro: Arduino Micro Microcontroller
